// Logisim project 7 segment.circ as structural Verilog: 1 circuit, main circuit main
module main (
  input  in_1,
  input  in_2,
  input  in_3,
  input  in_4
);

  wire and_1_out, and_2_out, and_3_out, and_4_out, and_5_out, and_6_out, and_7_out, and_8_out, and_9_out,
       and_10_out, and_11_out, and_12_out, and_13_out, and_14_out, and_15_out, and_16_out, nor_1_out,
       not_1_out, not_2_out, not_3_out, not_4_out, not_5_out, or_1_out, or_2_out, or_3_out, or_4_out,
       or_5_out, or_6_out, or_7_out, or_8_out, or_9_out, or_10_out, or_11_out, or_12_out, or_13_out,
       or_14_out, or_15_out;

  not not_1 (not_1_out, in_1);
  not not_2 (not_2_out, in_2);
  not not_3 (not_3_out, in_3);
  not not_4 (not_4_out, in_4);
  and and_1 (and_1_out, in_1, in_2);
  and and_2 (and_2_out, in_1, in_3);
  or or_1 (or_1_out, in_3, in_1, in_2);
  or or_2 (or_2_out, not_2_out, in_1, not_3_out, not_4_out);
  or or_3 (or_3_out, in_1, in_2, not_4_out);
  or or_4 (or_4_out, in_1, in_2, not_3_out, in_4);
  or or_5 (or_5_out, not_4_out, not_3_out, in_1, not_2_out);
  or or_6 (or_6_out, not_4_out, in_3, in_1, in_2);
  or or_7 (or_7_out, in_4, in_1, not_2_out, in_3);
  or or_8 (or_8_out, not_2_out, in_1, in_3, not_4_out);
  or or_9 (or_9_out, not_2_out, in_1, not_3_out, in_4);
  and and_3 (and_3_out, not_2_out, not_4_out);
  and and_4 (and_4_out, in_2, in_3, not_4_out);
  and and_5 (and_5_out, not_2_out, not_3_out, not_4_out);
  or or_10 (or_10_out, in_1, in_2, in_3, not_4_out);
  or or_11 (or_11_out, in_3, not_2_out, in_1, in_4);
  or or_12 (or_12_out, not_3_out, not_2_out, in_1, not_4_out);
  or or_13 (or_13_out, in_1, in_2, not_3_out, in_4);
  nor nor_1 (nor_1_out, and_2_out, and_1_out);
  and and_6 (and_6_out, or_1_out, or_2_out);
  and and_7 (and_7_out, or_3_out, or_4_out, or_5_out);
  and and_8 (and_8_out, or_6_out, or_7_out);
  and and_9 (and_9_out, or_8_out, or_9_out);
  or or_14 (or_14_out, and_3_out, and_4_out, and_5_out);
  and and_10 (and_10_out, or_10_out, or_11_out, or_12_out);
  and and_11 (and_11_out, nor_1_out, and_7_out);
  and and_12 (and_12_out, or_14_out, nor_1_out);
  and and_13 (and_13_out, nor_1_out, and_10_out);
  and and_14 (and_14_out, nor_1_out, or_13_out);
  not not_5 (not_5_out, nor_1_out);
  or or_15 (or_15_out, not_5_out, and_6_out);
  and and_15 (and_15_out, nor_1_out, and_9_out);
  _7_Segment_Display u_7_segment_display_1 (
    .g(or_15_out), .f(and_11_out), .a(and_16_out), .b(and_15_out), .e(and_12_out), .d(and_13_out),
    .c(and_14_out));  // open: dp
  and and_16 (and_16_out, and_8_out, nor_1_out);
  Multiplier multiplier_1 ();  // open: a, b, out, cin, cout
endmodule
