// Logisim project ALU einstieg.circ as structural Verilog: 1 circuit, main circuit main
module main (
  input  [7:0] a,
  input  [7:0] b,
  output [7:0] out_3,
  output [7:0] out_4,
  output [7:0] out_5,
  output [7:0] out_6,
  output [7:0] out_7,
  output [7:0] out_8,
  output [7:0] out_9,
  output [7:0] out_10,
  output out_11,
  output out_12,
  output out_13
);

  assign out_3 = a & b;  // AND_Gate and_1, 8 bits wide
  assign out_4 = ~(a & b);  // NAND_Gate nand_1, 8 bits wide
  assign out_5 = a | b;  // OR_Gate or_1, 8 bits wide
  assign out_6 = ~(a | b);  // NOR_Gate nor_1, 8 bits wide
  assign out_7 = a ^ b;  // XOR_Gate xor_1, 8 bits wide
  assign out_8 = ~(a ^ b);  // XNOR_Gate xnor_1, 8 bits wide
  Adder adder_1 (.a(a), .b(b), .out(out_9));  // open: cin, cout
  Subtractor subtractor_1 (.a(a), .b(b), .out(out_10));  // open: bin, bout
  Comparator comparator_1 (.a(a), .b(b), .gt(out_11), .eq(out_12), .lt(out_13));
endmodule
