// Logisim project ALU einstieg_2.circ as structural Verilog: 1 circuit, main circuit main
module main (
  input  [7:0] in_1,
  input  [7:0] in_2,
  input  [2:0] in_3,
  output [7:0] out_4
);

  wire [7:0] adder_1_out, and_1_out, multiplier_1_out, nand_1_out, nor_1_out, or_1_out, subtractor_1_out,
       xor_1_out;

  assign and_1_out = in_1 & in_2;  // AND_Gate and_1, 8 bits wide
  assign or_1_out = in_1 | in_2;  // OR_Gate or_1, 8 bits wide
  assign nand_1_out = ~(in_1 & in_2);  // NAND_Gate nand_1, 8 bits wide
  assign nor_1_out = ~(in_2 | in_1);  // NOR_Gate nor_1, 8 bits wide
  assign xor_1_out = in_2 ^ in_1;  // XOR_Gate xor_1, 8 bits wide
  Adder adder_1 (.a(in_1), .b(in_2), .out(adder_1_out));  // open: cin, cout
  Subtractor subtractor_1 (.a(in_2), .b(in_1), .out(subtractor_1_out));  // open: bin, bout
  Multiplier multiplier_1 (.a(in_2), .b(in_1), .out(multiplier_1_out));  // open: cin, cout
  Comparator comparator_1 (.a(in_1), .b(in_2));  // open: gt, eq, lt
  Multiplexer #(.select(3), .width(8)) multiplexer_1 (
    .in0(and_1_out), .in1(or_1_out), .in2(nand_1_out), .in3(nor_1_out), .in4(xor_1_out), .in5(adder_1_out),
    .in6(subtractor_1_out), .in7(multiplier_1_out), .out(out_4), .sel(in_3));  // open: en
endmodule
