// Logisim project Wuerfel.circ as structural Verilog: 1 circuit, main circuit main
module main (
  input  in_1,
  input  in_2,
  input  in_3,
  output out_4,
  output out_5,
  output out_6,
  output out_7,
  output out_8,
  output out_9,
  output out_10
);

  wire and_1_out, and_2_out, and_3_out, and_5_out, and_6_out, and_7_out, not_1_out, not_2_out, not_3_out,
       or_1_out, or_2_out, or_3_out;

  not not_1 (not_1_out, in_2);
  not not_2 (not_2_out, in_1);
  not not_3 (not_3_out, in_3);
  or or_1 (or_1_out, in_1, in_2, in_3);
  or or_2 (or_2_out, in_1, in_2, not_3_out);
  or or_3 (or_3_out, not_2_out, not_1_out, not_3_out);
  and and_1 (and_1_out, in_1, not_1_out, not_3_out);
  and and_2 (and_2_out, in_1, not_1_out, in_3);
  and and_3 (and_3_out, in_1, in_2, not_3_out);
  and and_4 (out_6, in_1, in_2, not_3_out);
  and and_5 (and_5_out, not_2_out, not_1_out, in_3);
  and and_6 (and_6_out, not_2_out, in_2, in_3);
  and and_7 (and_7_out, in_1, not_1_out, in_3);
  and and_8 (out_4, or_1_out, or_2_out, or_3_out);
  or or_4 (out_5, and_1_out, and_2_out, and_3_out);
  or or_5 (out_8, and_5_out, and_6_out, and_7_out);

  assign out_9 = out_5;
  assign out_10 = out_4;
endmodule
