// Logisim project allesFurTestWOWWW.circ as structural Verilog: 1 circuit, main circuit main
module main (
  input  S,
  input  in_2,
  input  R,
  input  S_2,
  input  in_5,
  input  R_2,
  input  in_7,
  input  S_3,
  input  R_3,
  input  S_4,
  input  in_11,
  input  S_5,
  input  R_4,
  input  in_14,
  input  in_15,
  input  S_6,
  input  R_5,
  input  zu_Beginn__Initialisierung,
  output out_19,
  output out_20,
  output out_21,
  output out_22,
  output Q,
  output nQ___P,
  output Q_2,
  output nQ___P_2,
  output Q_3,
  output nQ___P_3,
  output Q_4,
  output Q_5,
  output nQ___P_4,
  output Q_6,
  output nQ___P_5,
  output out_34
);

  wire a, adder_1_cout, adder_1_out, and_1_out, and_2_out, and_3_out, and_4_out, and_5_out, and_6_out,
       and_7_out, and_8_out, and_10_out, and_11_out, and_12_out, and_13_out, clock_1_out, clock_2_out,
       clock_3_out, clock_4_out, clock_5_out, clock_6_out, clock_7_out, clock_8_out, clock_9_out,
       clock_10_out, d_ff_1_q, d_ff_2_q, d_ff_3_q, d_ff_4_q, d_ff_5_q, d_ff_6_q, d_ff_7_q, d_ff_8_q,
       d_ff_9_q, d_ff_10_q, d_ff_11_q, d_ff_12_q, d_ff_13_q, d_ff_14_q, d_ff_15_q, d_ff_17_q, d_ff_18_q,
       d_ff_19_q, d_ff_20_q, d_ff_21_q, d_ff_22_q, d_ff_23_q, d_ff_24_q, d_ff_25_q, d_ff_26_q, d_ff_27_q,
       d_ff_28_q, d_ff_29_q, d_ff_30_q, d_ff_31_q, j_k_ff_1_q, j_k_ff_1_qn, j_k_ff_2_q, j_k_ff_2_qn,
       j_k_ff_3_q, j_k_ff_3_qn, j_k_ff_4_q, j_k_ff_4_qn, j_k_ff_5_q, j_k_ff_5_qn, j_k_ff_6_q, j_k_ff_6_qn,
       j_k_ff_7_q, j_k_ff_7_qn, j_k_ff_8_q, j_k_ff_12_qn, j_k_ff_13_qn, j_k_ff_14_q, j_k_ff_16_qn,
       j_k_ff_17_qn, j_k_ff_18_qn, j_k_ff_20_qn, j_k_ff_21_qn, j_k_ff_22_qn, j_k_ff_24_qn, j_k_ff_25_qn,
       j_k_ff_26_qn, j_k_ff_27_qn, j_k_ff_28_qn, j_k_ff_29_qn, j_k_ff_30_qn, j_k_ff_31_qn, j_k_ff_33_qn,
       nand_1_out, nand_2_out, nand_3_out, nand_4_out, nand_5_out, nand_6_out, nand_7_out, nand_8_out,
       nand_9_out, nand_10_out, nand_11_out, nand_12_out, nand_13_out, nand_15_out, nor_7_out, nor_8_out,
       nor_9_out, nor_10_out, not_1_out, not_2_out, not_3_out, not_4_out, not_5_out, not_6_out, not_7_out,
       or_1_out, Zahl_a_out, Zahl_b_out;

  Clock clock_1 (.out(clock_1_out));
  Clock clock_2 (.out(clock_2_out));
  Clock clock_3 (.out(clock_3_out));
  or or_1 (or_1_out, Q, S);
  not not_1 (not_1_out, R);
  nor nor_1 (nQ___P, S_2, Q_2);
  nor nor_2 (Q_2, nQ___P, R_2);
  and and_1 (and_1_out, S_3, clock_1_out);
  and and_2 (and_2_out, clock_1_out, R_3);
  and and_3 (and_3_out, S_4, clock_4_out);
  Clock clock_4 (.out(clock_4_out));
  and and_4 (and_4_out, clock_4_out, not_2_out);
  not not_2 (not_2_out, S_4);
  and and_5 (and_5_out, S_5, clock_2_out);
  and and_6 (and_6_out, clock_2_out, R_4);
  Pull_Resistor #(.pull(1)) pull_resistor_1 (.node(nQ___P_5));
  and and_7 (and_7_out, nQ___P_5, S_6, clock_3_out);
  and and_8 (and_8_out, clock_3_out, R_5, Q_6);
  Pull_Resistor #(.pull(1)) pull_resistor_2 (.node(Q_6));
  and and_9 (Q, or_1_out, not_1_out);
  nor nor_3 (nQ___P_2, and_1_out, Q_3);
  nor nor_4 (Q_3, nQ___P_2, and_2_out);
  nor nor_5 (nQ___P_3, and_3_out, Q_4);
  nor nor_6 (Q_4, nQ___P_3, and_4_out);
  nor nor_7 (nor_7_out, and_5_out, nor_8_out);
  nor nor_8 (nor_8_out, nor_7_out, and_6_out);
  nor nor_9 (nor_9_out, and_7_out, nor_10_out);
  nor nor_10 (nor_10_out, nor_9_out, and_8_out);
  and and_10 (and_10_out, not_3_out, nor_7_out);
  not not_3 (not_3_out, clock_2_out);
  and and_11 (and_11_out, nor_8_out, not_3_out);
  and and_12 (and_12_out, not_4_out, nor_9_out);
  not not_4 (not_4_out, clock_3_out);
  and and_13 (and_13_out, nor_10_out, not_4_out);
  nor nor_11 (Q_5, and_10_out, nQ___P_4);
  nor nor_12 (nQ___P_4, Q_5, and_11_out);
  nor nor_13 (Q_6, and_12_out, nQ___P_5);
  nor nor_14 (nQ___P_5, Q_6, and_13_out);
  Clock clock_5 (.out(clock_5_out));
  not not_5 (not_5_out, in_2);
  Clock clock_6 (.out(clock_6_out));
  D_Flip_Flop d_ff_1 (.clk(clock_6_out), .D(in_5), .Q(d_ff_1_q));  // open: Qn, preset, en, reset
  Shift_Register shift_register_1 (
    .shift(in_7), .clk(clock_7_out));  // open: in, out, load, clr, d0, q0, d1, q1, d2, q2, d3, q3, d4, q4, d5, q5, d6, q6, d7, q7
  Clock clock_7 (.out(clock_7_out));
  J_K_Flip_Flop j_k_ff_1 (
    .J(j_k_ff_2_q), .clk(clock_5_out), .K(j_k_ff_2_qn), .Q(j_k_ff_1_q), .Qn(j_k_ff_1_qn));  // open: preset, en, reset
  J_K_Flip_Flop j_k_ff_2 (
    .J(in_2), .clk(clock_5_out), .K(not_5_out), .Q(j_k_ff_2_q), .Qn(j_k_ff_2_qn));  // open: preset, en, reset
  D_Flip_Flop d_ff_2 (.clk(clock_6_out), .D(d_ff_1_q), .Q(d_ff_2_q));  // open: Qn, preset, en, reset
  J_K_Flip_Flop j_k_ff_3 (
    .J(j_k_ff_1_q), .clk(clock_5_out), .K(j_k_ff_1_qn), .Q(j_k_ff_3_q), .Qn(j_k_ff_3_qn));  // open: preset, en, reset
  D_Flip_Flop d_ff_3 (.clk(clock_6_out), .D(d_ff_2_q), .Q(d_ff_3_q));  // open: Qn, preset, en, reset
  Shift_Register Zahl_a (
    .in(in_11), .clk(clock_8_out), .out(Zahl_a_out));  // open: shift, load, clr, d0, q0, d1, q1, d2, q2, d3, q3, d4, q4, d5, q5, d6, q6, d7, q7
  Clock clock_8 (.out(clock_8_out));
  Shift_Register Zahl_b (
    .in(in_11), .clk(clock_8_out), .out(Zahl_b_out));  // open: shift, load, clr, d0, q0, d1, q1, d2, q2, d3, q3, d4, q4, d5, q5, d6, q6, d7, q7
  Clock clock_9 (.out(clock_9_out));
  J_K_Flip_Flop j_k_ff_4 (
    .J(j_k_ff_3_q), .clk(clock_5_out), .K(j_k_ff_3_qn), .Q(j_k_ff_4_q), .Qn(j_k_ff_4_qn));  // open: preset, en, reset
  D_Flip_Flop d_ff_4 (.clk(clock_6_out), .D(d_ff_5_q), .Q(d_ff_4_q));  // open: Qn, preset, en, reset
  D_Flip_Flop d_ff_5 (.clk(clock_6_out), .D(d_ff_3_q), .Q(d_ff_5_q));  // open: Qn, preset, en, reset
  D_Flip_Flop d_ff_6 (.clk(clock_9_out), .D(d_ff_7_q), .Q(d_ff_6_q));  // open: Qn, preset, en, reset
  D_Flip_Flop d_ff_7 (.clk(clock_9_out), .D(in_14), .Q(d_ff_7_q));  // open: Qn, preset, en, reset
  D_Flip_Flop d_ff_8 (.clk(clock_9_out), .D(in_15), .Q(d_ff_8_q));  // open: Qn, preset, en, reset
  D_Flip_Flop d_ff_9 (.clk(clock_9_out), .D(d_ff_8_q), .Q(d_ff_9_q));  // open: Qn, preset, en, reset
  J_K_Flip_Flop j_k_ff_5 (
    .J(j_k_ff_4_q), .clk(clock_5_out), .K(j_k_ff_4_qn), .Q(j_k_ff_5_q), .Qn(j_k_ff_5_qn));  // open: preset, en, reset
  J_K_Flip_Flop j_k_ff_6 (
    .J(j_k_ff_5_q), .clk(clock_5_out), .K(j_k_ff_5_qn), .Q(j_k_ff_6_q), .Qn(j_k_ff_6_qn));  // open: preset, en, reset
  D_Flip_Flop d_ff_10 (.clk(clock_6_out), .D(d_ff_4_q), .Q(d_ff_10_q));  // open: Qn, preset, en, reset
  Adder #(.width(1)) adder_1 (.a(Zahl_a_out), .b(Zahl_b_out), .out(adder_1_out), .cin(j_k_ff_8_q), .cout(adder_1_cout));
  Shift_Register Zahl_a_2 (
    .in(adder_1_out), .clk(clock_8_out));  // open: shift, out, load, clr, d0, q0, d1, q1, d2, q2, d3, q3, d4, q4, d5, q5, d6, q6, d7, q7
  not not_6 (not_6_out, adder_1_cout);
  D_Flip_Flop d_ff_11 (.clk(clock_9_out), .D(d_ff_6_q), .Q(d_ff_11_q));  // open: Qn, preset, en, reset
  D_Flip_Flop d_ff_12 (.clk(clock_9_out), .D(d_ff_9_q), .Q(d_ff_12_q));  // open: Qn, preset, en, reset
  J_K_Flip_Flop j_k_ff_7 (
    .J(j_k_ff_6_q), .clk(clock_5_out), .K(j_k_ff_6_qn), .Q(j_k_ff_7_q), .Qn(j_k_ff_7_qn));  // open: preset, en, reset
  D_Flip_Flop d_ff_13 (.clk(clock_6_out), .D(d_ff_10_q), .Q(d_ff_13_q));  // open: Qn, preset, en, reset
  J_K_Flip_Flop j_k_ff_8 (
    .J(adder_1_cout), .clk(clock_8_out), .K(not_6_out), .Q(j_k_ff_8_q));  // open: Qn, preset, en, reset
  D_Flip_Flop d_ff_14 (.clk(clock_9_out), .D(d_ff_11_q), .Q(d_ff_14_q));  // open: Qn, preset, en, reset
  D_Flip_Flop d_ff_15 (.clk(clock_9_out), .D(d_ff_12_q), .Q(d_ff_15_q));  // open: Qn, preset, en, reset
  J_K_Flip_Flop j_k_ff_9 (.J(j_k_ff_7_q), .clk(clock_5_out), .K(j_k_ff_7_qn));  // open: Q, Qn, preset, en, reset
  D_Flip_Flop d_ff_16 (.clk(clock_6_out), .D(d_ff_13_q));  // open: Q, Qn, preset, en, reset
  D_Flip_Flop d_ff_17 (.clk(clock_9_out), .D(d_ff_18_q), .Q(d_ff_17_q));  // open: Qn, preset, en, reset
  D_Flip_Flop d_ff_18 (.clk(clock_9_out), .D(d_ff_14_q), .Q(d_ff_18_q));  // open: Qn, preset, en, reset
  D_Flip_Flop d_ff_19 (.clk(clock_9_out), .D(d_ff_20_q), .Q(d_ff_19_q));  // open: Qn, preset, en, reset
  D_Flip_Flop d_ff_20 (.clk(clock_9_out), .D(d_ff_15_q), .Q(d_ff_20_q));  // open: Qn, preset, en, reset
  Clock clock_10 (.out(clock_10_out));
  D_Flip_Flop d_ff_21 (.clk(clock_9_out), .D(d_ff_17_q), .Q(d_ff_21_q));  // open: Qn, preset, en, reset
  D_Flip_Flop d_ff_22 (.clk(clock_9_out), .D(d_ff_19_q), .Q(d_ff_22_q));  // open: Qn, preset, en, reset
  J_K_Flip_Flop j_k_ff_10 (.J(1'b1), .clk(a), .K(1'b1), .Q(out_19));  // open: Qn, preset, en, reset
  Clock clock_11 (.out(a));
  J_K_Flip_Flop j_k_ff_11 (.J(1'b1), .clk(j_k_ff_16_qn), .K(1'b1));  // open: Q, Qn, preset, en, reset
  J_K_Flip_Flop j_k_ff_12 (.J(1'b1), .clk(clock_10_out), .K(1'b1), .Qn(j_k_ff_12_qn));  // open: Q, preset, en, reset
  J_K_Flip_Flop j_k_ff_13 (.J(1'b1), .clk(j_k_ff_33_qn), .K(1'b1), .Qn(j_k_ff_13_qn));  // open: Q, preset, en, reset
  D_Flip_Flop d_ff_23 (.clk(clock_9_out), .D(d_ff_21_q), .Q(d_ff_23_q));  // open: Qn, preset, en, reset
  D_Flip_Flop d_ff_24 (.clk(clock_9_out), .D(d_ff_22_q), .Q(d_ff_24_q));  // open: Qn, preset, en, reset
  J_K_Flip_Flop j_k_ff_14 (
    .J(out_34), .clk(clock_9_out), .K(not_7_out), .Q(j_k_ff_14_q));  // open: Qn, preset, en, reset
  not not_7 (not_7_out, out_34);
  J_K_Flip_Flop j_k_ff_15 (.J(1'b1), .clk(out_19), .K(1'b1), .Q(out_20));  // open: Qn, preset, en, reset
  J_K_Flip_Flop j_k_ff_16 (.J(1'b1), .clk(j_k_ff_20_qn), .K(1'b1), .Qn(j_k_ff_16_qn));  // open: Q, preset, en, reset
  J_K_Flip_Flop j_k_ff_17 (.J(1'b1), .clk(j_k_ff_12_qn), .K(1'b1), .Qn(j_k_ff_17_qn));  // open: Q, preset, en, reset
  J_K_Flip_Flop j_k_ff_18 (.J(1'b1), .clk(j_k_ff_13_qn), .K(1'b1), .Qn(j_k_ff_18_qn));  // open: Q, preset, en, reset
  nand nand_1 (nand_1_out, d_ff_23_q, d_ff_23_q);
  nand nand_2 (nand_2_out, d_ff_24_q, d_ff_24_q);
  nand nand_3 (nand_3_out, d_ff_23_q, d_ff_23_q);
  nand nand_4 (nand_4_out, j_k_ff_14_q, j_k_ff_14_q);
  nand nand_5 (nand_5_out, d_ff_24_q, d_ff_24_q);
  nand nand_6 (nand_6_out, j_k_ff_14_q, j_k_ff_14_q);
  nand nand_7 (nand_7_out, d_ff_24_q, j_k_ff_14_q);
  nand nand_8 (nand_8_out, d_ff_23_q, j_k_ff_14_q);
  nand nand_9 (nand_9_out, d_ff_23_q, d_ff_24_q);
  J_K_Flip_Flop j_k_ff_19 (.J(1'b1), .clk(out_20), .K(1'b1), .Q(out_21));  // open: Qn, preset, en, reset
  J_K_Flip_Flop j_k_ff_20 (.J(1'b1), .clk(j_k_ff_24_qn), .K(1'b1), .Qn(j_k_ff_20_qn));  // open: Q, preset, en, reset
  J_K_Flip_Flop j_k_ff_21 (.J(1'b1), .clk(j_k_ff_17_qn), .K(1'b1), .Qn(j_k_ff_21_qn));  // open: Q, preset, en, reset
  J_K_Flip_Flop j_k_ff_22 (.J(1'b1), .clk(j_k_ff_18_qn), .K(1'b1), .Qn(j_k_ff_22_qn));  // open: Q, preset, en, reset
  nand nand_10 (nand_10_out, nand_1_out, nand_2_out, j_k_ff_14_q);
  nand nand_11 (nand_11_out, nand_3_out, d_ff_24_q, nand_4_out);
  nand nand_12 (nand_12_out, d_ff_23_q, nand_5_out, nand_6_out);
  nand nand_13 (nand_13_out, d_ff_23_q, d_ff_24_q, j_k_ff_14_q);
  nand nand_14 (out_34, nand_7_out, nand_8_out, nand_9_out);
  J_K_Flip_Flop j_k_ff_23 (.J(1'b1), .clk(out_21), .K(1'b1), .Q(out_22));  // open: Qn, preset, en, reset
  J_K_Flip_Flop j_k_ff_24 (.J(1'b1), .clk(a), .K(1'b1), .Qn(j_k_ff_24_qn));  // open: Q, preset, en, reset
  J_K_Flip_Flop j_k_ff_25 (.J(1'b1), .clk(j_k_ff_26_qn), .K(1'b1), .Qn(j_k_ff_25_qn));  // open: Q, preset, en, reset
  J_K_Flip_Flop j_k_ff_26 (.J(1'b1), .clk(j_k_ff_21_qn), .K(1'b1), .Qn(j_k_ff_26_qn));  // open: Q, preset, en, reset
  J_K_Flip_Flop j_k_ff_27 (.J(1'b1), .clk(j_k_ff_22_qn), .K(1'b1), .Qn(j_k_ff_27_qn));  // open: Q, preset, en, reset
  J_K_Flip_Flop j_k_ff_28 (.J(1'b1), .clk(j_k_ff_27_qn), .K(1'b1), .Qn(j_k_ff_28_qn));  // open: Q, preset, en, reset
  nand nand_15 (nand_15_out, nand_10_out, nand_11_out, nand_12_out, nand_13_out);
  J_K_Flip_Flop j_k_ff_29 (.J(1'b1), .clk(j_k_ff_25_qn), .K(1'b1), .Qn(j_k_ff_29_qn));  // open: Q, preset, en, reset
  J_K_Flip_Flop j_k_ff_30 (.J(1'b1), .clk(j_k_ff_28_qn), .K(1'b1), .Qn(j_k_ff_30_qn));  // open: Q, preset, en, reset
  D_Flip_Flop d_ff_25 (.clk(clock_9_out), .D(d_ff_26_q), .Q(d_ff_25_q));  // open: Qn, preset, en, reset
  D_Flip_Flop d_ff_26 (.clk(clock_9_out), .D(nand_15_out), .Q(d_ff_26_q));  // open: Qn, preset, en, reset
  J_K_Flip_Flop j_k_ff_31 (.J(1'b1), .clk(j_k_ff_29_qn), .K(1'b1), .Qn(j_k_ff_31_qn));  // open: Q, preset, en, reset
  J_K_Flip_Flop j_k_ff_32 (.J(1'b1), .clk(j_k_ff_30_qn), .K(1'b1));  // open: Q, Qn, preset, en, reset
  D_Flip_Flop d_ff_27 (.clk(clock_9_out), .D(d_ff_25_q), .Q(d_ff_27_q));  // open: Qn, preset, en, reset
  J_K_Flip_Flop j_k_ff_33 (.J(1'b1), .clk(j_k_ff_31_qn), .K(1'b1), .Qn(j_k_ff_33_qn));  // open: Q, preset, en, reset
  D_Flip_Flop d_ff_28 (.clk(clock_9_out), .D(d_ff_27_q), .Q(d_ff_28_q));  // open: Qn, preset, en, reset
  D_Flip_Flop d_ff_29 (.clk(clock_9_out), .D(d_ff_28_q), .Q(d_ff_29_q));  // open: Qn, preset, en, reset
  D_Flip_Flop d_ff_30 (.clk(clock_9_out), .D(d_ff_29_q), .Q(d_ff_30_q));  // open: Qn, preset, en, reset
  D_Flip_Flop d_ff_31 (.clk(clock_9_out), .D(d_ff_30_q), .Q(d_ff_31_q));  // open: Qn, preset, en, reset
  D_Flip_Flop d_ff_32 (.clk(clock_9_out), .D(d_ff_31_q));  // open: Q, Qn, preset, en, reset

  // Notes on the sheet:
  //   alle Flipflops
  //   1. Einweg-Flipflop
  //   2. RS-Flipflop
  //   4. D-Flipflop
  //   5. MS-Flipflop
  //   6. JK-Flipflop
  //   3. taktg. RS-Flipflop
  //   Master
  //   ------------------------------------------------
  //   Slave
  //   ------------------------------------------------
  //   Schieberegister
  //   1. JK-Schieberegister
  //   2. D-Schieberegister
  //   3. kompakter Schieberegister
  //   serieller Addierer
  //   1. kompakt Addierer
  //   2. ausführlicher Addierer
  //   Zähler
endmodule
