// Logisim project andxor.circ as structural Verilog: 1 circuit, main circuit main
module main (
  input  a,
  output konstante_0,
  output nicht_a,
  output a_2,
  output konstante_1
);

  not not_1 (nicht_a, a);
  and and_1 (konstante_0, nicht_a, a);
  or or_1 (konstante_1, nicht_a, a);

  assign a_2 = a;
endmodule
