// Logisim project asynchroner zaehler.circ as structural Verilog: 1 circuit, main circuit main
module main (
  input  in_1,
  input  in_2,
  output out_3,
  output out_4,
  output out_5,
  output out_6,
  output out_7,
  output out_8,
  output out_9,
  output out_10,
  output out_11,
  output out_12,
  output out_13,
  output out_14,
  output out_15,
  output out_16,
  output out_17,
  output out_18,
  output out_19,
  output out_20,
  output out_21,
  output out_22,
  output out_23
);

  wire and_1_out, and_2_out, and_3_out, and_4_out, and_5_out, and_6_out, and_7_out, and_8_out, clock_1_out,
       clock_2_out, clock_3_out, j_k_ff_4_qn, j_k_ff_5_q, j_k_ff_6_q, j_k_ff_8_q, j_k_ff_9_q, j_k_ff_11_qn,
       j_k_ff_12_q, j_k_ff_13_q, j_k_ff_14_q, j_k_ff_16_qn, j_k_ff_17_q, j_k_ff_18_q, j_k_ff_19_q,
       j_k_ff_20_q, j_k_ff_21_q, t_ff_3_q, t_ff_4_q, t_ff_5_q, t_ff_6_q, t_ff_8_q, t_ff_9_q, t_ff_10_q,
       t_ff_11_q, t_ff_13_q, t_ff_14_q, t_ff_15_q, t_ff_16_q, t_ff_18_q, t_ff_19_q, t_ff_20_q, t_ff_21_q,
       t_ff_23_q, t_ff_24_q, t_ff_25_q, t_ff_26_q, t_ff_28_q, t_ff_29_q, t_ff_30_q, t_ff_31_q, t_ff_33_q,
       t_ff_34_q, t_ff_35_q, t_ff_36_q, t_ff_38_q, t_ff_39_q, t_ff_40_q, t_ff_41_q, t_ff_43_q, t_ff_44_q,
       t_ff_45_q, t_ff_46_q, t_ff_48_q, t_ff_49_q, t_ff_50_q, t_ff_51_q, t_ff_53_q, t_ff_54_q, t_ff_55_q,
       t_ff_56_q, t_ff_58_q, t_ff_59_q, t_ff_60_q, t_ff_61_q;

  Clock clock_1 (.out(clock_1_out));
  Clock clock_2 (.out(clock_2_out));
  Clock clock_3 (.out(clock_3_out));
  and and_1 (and_1_out, and_4_out, j_k_ff_8_q);
  T_Flip_Flop t_ff_1 (.clk(clock_2_out), .T(in_1), .Q(out_3));  // open: Qn, preset, reset, en
  J_K_Flip_Flop j_k_ff_1 (.J(1'b1), .clk(out_19), .K(1'b1), .Q(out_18));  // open: Qn, preset, en, reset
  J_K_Flip_Flop j_k_ff_2 (.J(1'b1), .clk(clock_1_out), .K(1'b1), .Q(out_19));  // open: Qn, preset, en, reset
  J_K_Flip_Flop j_k_ff_3 (.J(1'b1), .clk(j_k_ff_4_qn), .K(1'b1));  // open: Q, Qn, preset, en, reset
  J_K_Flip_Flop j_k_ff_4 (.J(1'b1), .clk(j_k_ff_11_qn), .K(1'b1), .Qn(j_k_ff_4_qn));  // open: Q, preset, en, reset
  J_K_Flip_Flop j_k_ff_5 (
    .J(j_k_ff_6_q), .clk(clock_1_out), .K(j_k_ff_6_q), .Q(j_k_ff_5_q), .reset(j_k_ff_13_q));  // open: Qn, preset, en
  J_K_Flip_Flop j_k_ff_6 (
    .J(1'b1), .clk(clock_1_out), .K(1'b1), .Q(j_k_ff_6_q), .reset(j_k_ff_13_q));  // open: Qn, preset, en
  and and_2 (and_2_out, j_k_ff_6_q, j_k_ff_17_q);
  J_K_Flip_Flop j_k_ff_7 (.J(and_1_out), .clk(clock_1_out), .K(and_1_out), .Qn(out_20));  // open: Q, preset, en, reset
  J_K_Flip_Flop j_k_ff_8 (
    .J(and_4_out), .clk(clock_1_out), .K(and_4_out), .Q(j_k_ff_8_q), .Qn(out_21));  // open: preset, en, reset
  T_Flip_Flop t_ff_2 (.clk(out_3), .T(out_3), .Q(out_4));  // open: Qn, preset, reset, en
  T_Flip_Flop t_ff_3 (.clk(out_15), .T(out_15), .Q(t_ff_3_q));  // open: Qn, preset, reset, en
  T_Flip_Flop t_ff_4 (.clk(t_ff_58_q), .T(t_ff_58_q), .Q(t_ff_4_q));  // open: Qn, preset, reset, en
  T_Flip_Flop t_ff_5 (.clk(t_ff_59_q), .T(t_ff_59_q), .Q(t_ff_5_q));  // open: Qn, preset, reset, en
  T_Flip_Flop t_ff_6 (.clk(t_ff_60_q), .T(t_ff_60_q), .Q(t_ff_6_q));  // open: Qn, preset, reset, en
  J_K_Flip_Flop j_k_ff_9 (.J(in_1), .clk(clock_3_out), .K(in_1), .Q(j_k_ff_9_q));  // open: Qn, preset, en, reset
  J_K_Flip_Flop j_k_ff_10 (.J(1'b1), .clk(out_18), .K(1'b1), .Q(out_17));  // open: Qn, preset, en, reset
  J_K_Flip_Flop j_k_ff_11 (.J(1'b1), .clk(j_k_ff_16_qn), .K(1'b1), .Qn(j_k_ff_11_qn));  // open: Q, preset, en, reset
  and and_3 (and_3_out, j_k_ff_6_q, j_k_ff_5_q);
  J_K_Flip_Flop j_k_ff_12 (
    .J(and_3_out), .clk(clock_1_out), .K(and_3_out), .Q(j_k_ff_12_q), .reset(j_k_ff_13_q));  // open: Qn, preset, en
  J_K_Flip_Flop j_k_ff_13 (
    .J(and_2_out), .clk(clock_1_out), .K(j_k_ff_13_q), .Q(j_k_ff_13_q));  // open: Qn, preset, en, reset
  and and_4 (and_4_out, j_k_ff_18_q, j_k_ff_14_q);
  J_K_Flip_Flop j_k_ff_14 (
    .J(j_k_ff_18_q), .clk(clock_1_out), .K(j_k_ff_18_q), .Q(j_k_ff_14_q), .Qn(out_22));  // open: preset, en, reset
  T_Flip_Flop t_ff_7 (.clk(out_4), .T(out_4), .Q(out_5));  // open: Qn, preset, reset, en
  T_Flip_Flop t_ff_8 (.clk(t_ff_3_q), .T(t_ff_3_q), .Q(t_ff_8_q));  // open: Qn, preset, reset, en
  T_Flip_Flop t_ff_9 (.clk(t_ff_4_q), .T(t_ff_4_q), .Q(t_ff_9_q));  // open: Qn, preset, reset, en
  T_Flip_Flop t_ff_10 (.clk(t_ff_5_q), .T(t_ff_5_q), .Q(t_ff_10_q));  // open: Qn, preset, reset, en
  T_Flip_Flop t_ff_11 (.clk(t_ff_6_q), .T(t_ff_6_q), .Q(t_ff_11_q));  // open: Qn, preset, reset, en
  J_K_Flip_Flop j_k_ff_15 (.J(1'b1), .clk(out_17), .K(1'b1), .Q(out_16));  // open: Qn, preset, en, reset
  J_K_Flip_Flop j_k_ff_16 (.J(1'b1), .clk(clock_1_out), .K(1'b1), .Qn(j_k_ff_16_qn));  // open: Q, preset, en, reset
  J_K_Flip_Flop j_k_ff_17 (
    .J(and_5_out), .clk(clock_1_out), .K(and_5_out), .Q(j_k_ff_17_q), .reset(j_k_ff_13_q));  // open: Qn, preset, en
  and and_5 (and_5_out, j_k_ff_12_q, j_k_ff_6_q, j_k_ff_5_q);
  J_K_Flip_Flop j_k_ff_18 (
    .J(1'b1), .clk(clock_1_out), .K(1'b1), .Q(j_k_ff_18_q), .Qn(out_23));  // open: preset, en, reset
  T_Flip_Flop t_ff_12 (.clk(out_5), .T(out_5), .Q(out_6));  // open: Qn, preset, reset, en
  T_Flip_Flop t_ff_13 (.clk(t_ff_8_q), .T(t_ff_8_q), .Q(t_ff_13_q));  // open: Qn, preset, reset, en
  T_Flip_Flop t_ff_14 (.clk(t_ff_9_q), .T(t_ff_9_q), .Q(t_ff_14_q));  // open: Qn, preset, reset, en
  T_Flip_Flop t_ff_15 (.clk(t_ff_10_q), .T(t_ff_10_q), .Q(t_ff_15_q));  // open: Qn, preset, reset, en
  T_Flip_Flop t_ff_16 (.clk(t_ff_11_q), .T(t_ff_11_q), .Q(t_ff_16_q));  // open: Qn, preset, reset, en
  J_K_Flip_Flop j_k_ff_19 (
    .J(j_k_ff_9_q), .clk(clock_3_out), .K(j_k_ff_9_q), .Q(j_k_ff_19_q));  // open: Qn, preset, en, reset
  and and_6 (and_6_out, j_k_ff_19_q, j_k_ff_9_q);
  T_Flip_Flop t_ff_17 (.clk(out_6), .T(out_6), .Q(out_7));  // open: Qn, preset, reset, en
  T_Flip_Flop t_ff_18 (.clk(t_ff_13_q), .T(t_ff_13_q), .Q(t_ff_18_q));  // open: Qn, preset, reset, en
  T_Flip_Flop t_ff_19 (.clk(t_ff_14_q), .T(t_ff_14_q), .Q(t_ff_19_q));  // open: Qn, preset, reset, en
  T_Flip_Flop t_ff_20 (.clk(t_ff_15_q), .T(t_ff_15_q), .Q(t_ff_20_q));  // open: Qn, preset, reset, en
  T_Flip_Flop t_ff_21 (.clk(t_ff_16_q), .T(t_ff_16_q), .Q(t_ff_21_q));  // open: Qn, preset, reset, en
  J_K_Flip_Flop j_k_ff_20 (
    .J(and_6_out), .clk(clock_3_out), .K(and_6_out), .Q(j_k_ff_20_q));  // open: Qn, preset, en, reset
  T_Flip_Flop t_ff_22 (.clk(out_7), .T(out_7), .Q(out_8));  // open: Qn, preset, reset, en
  T_Flip_Flop t_ff_23 (.clk(t_ff_18_q), .T(t_ff_18_q), .Q(t_ff_23_q));  // open: Qn, preset, reset, en
  T_Flip_Flop t_ff_24 (.clk(t_ff_19_q), .T(t_ff_19_q), .Q(t_ff_24_q));  // open: Qn, preset, reset, en
  T_Flip_Flop t_ff_25 (.clk(t_ff_20_q), .T(t_ff_20_q), .Q(t_ff_25_q));  // open: Qn, preset, reset, en
  T_Flip_Flop t_ff_26 (.clk(t_ff_21_q), .T(t_ff_21_q), .Q(t_ff_26_q));  // open: Qn, preset, reset, en
  J_K_Flip_Flop j_k_ff_21 (
    .J(and_7_out), .clk(clock_3_out), .K(and_7_out), .Q(j_k_ff_21_q));  // open: Qn, preset, en, reset
  and and_7 (and_7_out, j_k_ff_20_q, and_6_out);
  T_Flip_Flop t_ff_27 (.clk(out_8), .T(out_8), .Q(out_9));  // open: Qn, preset, reset, en
  T_Flip_Flop t_ff_28 (.clk(t_ff_23_q), .T(t_ff_23_q), .Q(t_ff_28_q));  // open: Qn, preset, reset, en
  T_Flip_Flop t_ff_29 (.clk(t_ff_24_q), .T(t_ff_24_q), .Q(t_ff_29_q));  // open: Qn, preset, reset, en
  T_Flip_Flop t_ff_30 (.clk(t_ff_25_q), .T(t_ff_25_q), .Q(t_ff_30_q));  // open: Qn, preset, reset, en
  T_Flip_Flop t_ff_31 (.clk(t_ff_26_q), .T(t_ff_26_q), .Q(t_ff_31_q));  // open: Qn, preset, reset, en
  and and_8 (and_8_out, j_k_ff_21_q, and_7_out);
  T_Flip_Flop t_ff_32 (.clk(out_9), .T(out_9), .Q(out_10));  // open: Qn, preset, reset, en
  Clock clock_4 ();  // open: out
  T_Flip_Flop t_ff_33 (.clk(t_ff_28_q), .T(t_ff_28_q), .Q(t_ff_33_q));  // open: Qn, preset, reset, en
  T_Flip_Flop t_ff_34 (.clk(t_ff_29_q), .T(t_ff_29_q), .Q(t_ff_34_q));  // open: Qn, preset, reset, en
  T_Flip_Flop t_ff_35 (.clk(t_ff_30_q), .T(t_ff_30_q), .Q(t_ff_35_q));  // open: Qn, preset, reset, en
  T_Flip_Flop t_ff_36 (.clk(t_ff_31_q), .T(t_ff_31_q), .Q(t_ff_36_q));  // open: Qn, preset, reset, en
  J_K_Flip_Flop j_k_ff_22 (.J(and_8_out), .clk(clock_3_out), .K(and_8_out));  // open: Q, Qn, preset, en, reset
  T_Flip_Flop t_ff_37 (.clk(out_10), .T(out_10), .Q(out_11));  // open: Qn, preset, reset, en
  T_Flip_Flop t_ff_38 (.clk(t_ff_33_q), .T(t_ff_33_q), .Q(t_ff_38_q));  // open: Qn, preset, reset, en
  T_Flip_Flop t_ff_39 (.clk(t_ff_34_q), .T(t_ff_34_q), .Q(t_ff_39_q));  // open: Qn, preset, reset, en
  T_Flip_Flop t_ff_40 (.clk(t_ff_35_q), .T(t_ff_35_q), .Q(t_ff_40_q));  // open: Qn, preset, reset, en
  T_Flip_Flop t_ff_41 (.clk(t_ff_36_q), .T(t_ff_36_q), .Q(t_ff_41_q));  // open: Qn, preset, reset, en
  T_Flip_Flop t_ff_42 (.clk(out_11), .T(out_11), .Q(out_12));  // open: Qn, preset, reset, en
  T_Flip_Flop t_ff_43 (.clk(t_ff_38_q), .T(t_ff_38_q), .Q(t_ff_43_q));  // open: Qn, preset, reset, en
  T_Flip_Flop t_ff_44 (.clk(t_ff_39_q), .T(t_ff_39_q), .Q(t_ff_44_q));  // open: Qn, preset, reset, en
  T_Flip_Flop t_ff_45 (.clk(t_ff_40_q), .T(t_ff_40_q), .Q(t_ff_45_q));  // open: Qn, preset, reset, en
  T_Flip_Flop t_ff_46 (.clk(t_ff_41_q), .T(t_ff_41_q), .Q(t_ff_46_q));  // open: Qn, preset, reset, en
  T_Flip_Flop t_ff_47 (.clk(out_12), .T(out_12), .Q(out_13));  // open: Qn, preset, reset, en
  T_Flip_Flop t_ff_48 (.clk(t_ff_43_q), .T(t_ff_43_q), .Q(t_ff_48_q));  // open: Qn, preset, reset, en
  T_Flip_Flop t_ff_49 (.clk(t_ff_44_q), .T(t_ff_44_q), .Q(t_ff_49_q));  // open: Qn, preset, reset, en
  T_Flip_Flop t_ff_50 (.clk(t_ff_45_q), .T(t_ff_45_q), .Q(t_ff_50_q));  // open: Qn, preset, reset, en
  T_Flip_Flop t_ff_51 (.clk(t_ff_46_q), .T(t_ff_46_q), .Q(t_ff_51_q));  // open: Qn, preset, reset, en
  T_Flip_Flop t_ff_52 (.clk(out_13), .T(out_13), .Q(out_14));  // open: Qn, preset, reset, en
  T_Flip_Flop t_ff_53 (.clk(t_ff_48_q), .T(t_ff_48_q), .Q(t_ff_53_q));  // open: Qn, preset, reset, en
  T_Flip_Flop t_ff_54 (.clk(t_ff_49_q), .T(t_ff_49_q), .Q(t_ff_54_q));  // open: Qn, preset, reset, en
  T_Flip_Flop t_ff_55 (.clk(t_ff_50_q), .T(t_ff_50_q), .Q(t_ff_55_q));  // open: Qn, preset, reset, en
  T_Flip_Flop t_ff_56 (.clk(t_ff_51_q), .T(t_ff_51_q), .Q(t_ff_56_q));  // open: Qn, preset, reset, en
  T_Flip_Flop t_ff_57 (.clk(out_14), .T(out_14), .Q(out_15));  // open: Qn, preset, reset, en
  T_Flip_Flop t_ff_58 (.clk(t_ff_53_q), .T(t_ff_53_q), .Q(t_ff_58_q));  // open: Qn, preset, reset, en
  T_Flip_Flop t_ff_59 (.clk(t_ff_54_q), .T(t_ff_54_q), .Q(t_ff_59_q));  // open: Qn, preset, reset, en
  T_Flip_Flop t_ff_60 (.clk(t_ff_55_q), .T(t_ff_55_q), .Q(t_ff_60_q));  // open: Qn, preset, reset, en
  T_Flip_Flop t_ff_61 (.clk(t_ff_56_q), .T(t_ff_56_q), .Q(t_ff_61_q));  // open: Qn, preset, reset, en

  // Notes on the sheet:
  //   Asynchroner Downcounter
  //   Asynchroner Upcounter
  //   SYNCHRONE ZAEHLER
endmodule
