// Logisim project binaereOperATOREN.circ as structural Verilog: 1 circuit, main circuit main
module main (
  input  a,
  input  b,
  output konst_0,
  output konst_0_2,
  output NOR,
  output NOR_2,
  output nicht_b__a,
  output out_8,
  output nicht_a,
  output out_10,
  output out_11,
  output nicht_a__b,
  output out_13,
  output nicht_b,
  output XOR,
  output NAND,
  output AND,
  output XNOR,
  output b_2,
  output a__b,
  output a_2,
  output b__a,
  output OR,
  output konst_1
);

  wire and_1_out, and_2_out, and_7_out, and_9_out, and_10_out, and_11_out, nand_1_out, nand_2_out,
       nand_3_out, nand_4_out, nand_5_out, nand_6_out, nand_7_out, nand_8_out, nand_9_out, nand_10_out,
       nand_13_out, nand_16_out, nand_17_out, nand_18_out, nand_19_out, nand_20_out, nand_21_out,
       nand_22_out, nand_23_out, nand_24_out, not_3_out, not_4_out, or_1_out, or_2_out, or_3_out, xnor_1_out,
       xnor_2_out, xnor_3_out;

  not not_1 (nicht_a, a);
  not not_2 (nicht_b, b);
  or or_1 (or_1_out, a, b);
  and and_1 (and_1_out, b, a);
  or or_2 (or_2_out, a, b);
  and and_2 (and_2_out, b, a);
  and and_3 (konst_0, nicht_a, a);
  or or_3 (or_3_out, a, b);
  and and_4 (nicht_b__a, nicht_a, b);
  and and_5 (nicht_a__b, a, nicht_b);
  and and_6 (XOR, or_1_out, not_3_out);
  not not_3 (not_3_out, and_1_out);
  and and_7 (and_7_out, b, a);
  and and_8 (AND, b, a);
  and and_9 (and_9_out, or_2_out, not_4_out);
  not not_4 (not_4_out, and_2_out);
  and and_10 (and_10_out, a, nicht_b);
  and and_11 (and_11_out, nicht_a, b);
  or or_4 (OR, b, a);
  or or_5 (konst_1, a, nicht_a);
  not not_5 (NOR, or_3_out);
  not not_6 (NAND, and_7_out);
  not not_7 (XNOR, and_9_out);
  not not_8 (a__b, and_10_out);
  not not_9 (b__a, and_11_out);
  not not_10 (out_10, a);
  not not_11 (out_13, b);
  nand nand_1 (nand_1_out, a, out_10);
  nand nand_2 (nand_2_out, a, a);
  nand nand_3 (nand_3_out, b, b);
  nand nand_4 (nand_4_out, b, out_10);
  nand nand_5 (nand_5_out, a, out_13);
  nand nand_6 (nand_6_out, a, a);
  nand nand_7 (nand_7_out, b, b);
  nand nand_8 (nand_8_out, b, a);
  nand nand_9 (nand_9_out, a, a);
  nand nand_10 (nand_10_out, b, b);
  // NAND_Gate nand_11 has open pins: in0=a, in1=out_13, out=open
  nand nand_12 (konst_0_2, nand_1_out, nand_1_out);
  nand nand_13 (nand_13_out, nand_2_out, nand_3_out);
  nand nand_14 (out_8, nand_4_out, nand_4_out);
  nand nand_15 (out_11, nand_5_out, nand_5_out);
  nand nand_16 (nand_16_out, nand_6_out, nand_7_out);
  nand nand_17 (nand_17_out, nand_16_out, nand_18_out);
  nand nand_18 (nand_18_out, b, a);
  nand nand_19 (nand_19_out, b, a);
  nand nand_20 (nand_20_out, nand_8_out, nand_8_out);
  nand nand_21 (nand_21_out, nand_9_out, nand_10_out);
  nand nand_22 (nand_22_out, nand_21_out, nand_23_out);
  nand nand_23 (nand_23_out, b, a);
  not not_12 (NOR_2, nand_13_out);
  nand nand_24 (nand_24_out, nand_17_out, nand_17_out);
  xnor xnor_1 (xnor_1_out, konst_0, konst_0_2);
  xnor xnor_2 (xnor_2_out, NOR, NOR_2);
  xnor xnor_3 (xnor_3_out, nicht_b__a, out_8);

  assign a_2 = a;
  assign b_2 = b;
endmodule
