// Logisim project colaautomat.circ as structural Verilog: 1 circuit, main circuit main
module main (
  input  Eingabe,
  output Cola,
  output f50,
  output f100,
  output f150
);

  wire a_q, a_qn, and_1_out, and_2_out, and_3_out, and_4_out, and_5_out, and_6_out, and_7_out, b_q, b_qn,
       clock_1_out, j_k_ff_1_q, j_k_ff_1_qn, j_k_ff_2_q, j_k_ff_2_qn, not_1_out, not_2_out, not_3_out,
       not_4_out, not_5_out, or_1_out, or_2_out, or_3_out, or_4_out, or_5_out, or_6_out;

  Clock clock_1 (.out(clock_1_out));
  not not_1 (not_1_out, Eingabe);
  not not_2 (not_2_out, or_1_out);
  J_K_Flip_Flop a (.J(or_1_out), .clk(clock_1_out), .K(not_2_out), .Q(a_q), .Qn(a_qn));  // open: preset, en, reset
  J_K_Flip_Flop b (.J(or_2_out), .clk(clock_1_out), .K(not_3_out), .Q(b_q), .Qn(b_qn));  // open: preset, en, reset
  not not_3 (not_3_out, or_2_out);
  and and_1 (and_1_out, a_qn, b_q);
  or or_1 (or_1_out, and_1_out, and_2_out, and_3_out);
  and and_2 (and_2_out, Eingabe, a_qn);
  and and_3 (and_3_out, a_q, b_qn, not_1_out);
  and and_4 (and_4_out, b_qn, not_1_out);
  or or_2 (or_2_out, and_4_out, and_5_out);
  and and_5 (and_5_out, a_qn, b_q, Eingabe);
  or or_3 (or_3_out, a_q, b_q);
  and and_6 (and_6_out, or_3_out, or_4_out);
  or or_4 (or_4_out, a_q, Eingabe);
  or or_5 (or_5_out, b_q, Eingabe);
  and and_7 (and_7_out, or_5_out, or_6_out);
  or or_6 (or_6_out, a_q, b_qn, not_1_out);
  J_K_Flip_Flop j_k_ff_1 (
    .J(and_6_out), .clk(clock_1_out), .K(not_4_out), .Q(j_k_ff_1_q), .Qn(j_k_ff_1_qn));  // open: preset, en, reset
  not not_4 (not_4_out, and_6_out);
  J_K_Flip_Flop j_k_ff_2 (
    .J(and_7_out), .clk(clock_1_out), .K(not_5_out), .Q(j_k_ff_2_q), .Qn(j_k_ff_2_qn));  // open: preset, en, reset
  not not_5 (not_5_out, and_7_out);
  and and_8 (Cola, j_k_ff_1_q, j_k_ff_2_q);
  and and_9 (f50, j_k_ff_1_q, j_k_ff_2_qn);
  and and_10 (f150, j_k_ff_1_qn, j_k_ff_2_qn);
  and and_11 (f100, j_k_ff_2_q, j_k_ff_1_qn);
endmodule
