// Logisim project durch8erkenner.circ as structural Verilog: 1 circuit, main circuit main
module main (
  input  in_1,
  input  in_2,
  input  in_3,
  input  in_4,
  input  in_5,
  input  in_6,
  input  in_7,
  input  in_8,
  input  in_9,
  input  in_10,
  output out_11
);

  wire or_1_out;

  or or_1 (or_1_out, in_1, in_2, in_3, in_4, in_5, in_6, in_7, in_8, in_9, in_10);
  and and_1 (out_11, ~in_10, ~in_9, ~in_8, or_1_out);  // AND_Gate
endmodule
