// Logisim project emma.circ as structural Verilog: 1 circuit, main circuit main
module main (
  input  a,
  input  b,
  input  c,
  output L1,
  output L2,
  output L3,
  output L4
);

  wire and_1_out, and_2_out, and_3_out, and_4_out, and_5_out, not_1_out, not_2_out, not_3_out, or_1_out,
       or_2_out, or_3_out;

  not not_1 (not_1_out, a);
  not not_2 (not_2_out, b);
  not not_3 (not_3_out, c);
  or or_1 (or_1_out, a, b, c);
  or or_2 (or_2_out, a, not_2_out, not_3_out);
  or or_3 (or_3_out, not_1_out, not_2_out, not_3_out);
  and and_1 (and_1_out, not_1_out, not_2_out, c);
  and and_2 (and_2_out, not_1_out, b, c);
  and and_3 (and_3_out, a, not_2_out, not_3_out);
  and and_4 (and_4_out, a, b, c);
  and and_5 (and_5_out, not_1_out, not_2_out, not_3_out);
  and and_6 (L1, or_1_out, or_2_out, or_3_out);
  or or_4 (L2, and_1_out, and_2_out, and_3_out);
  or or_5 (L3, not_1_out, a);
  or or_6 (L4, and_4_out, and_5_out);
endmodule
