// Logisim project flipflops.circ as structural Verilog: 1 circuit, main circuit main
module main (
  input  in_1,
  input  in_2,
  output out_3,
  output out_4,
  output Q,
  output Nicht_Q,
  output Niht_Q,
  output Q_2,
  output Niht_Q_2,
  output Q_3
);

  wire and_2_out, and_3_out, clock_1_out, not_1_out, or_2_out;

  or or_1 (out_3, out_3, in_1);
  or or_2 (or_2_out, in_1, out_4);
  not not_1 (not_1_out, in_2);
  Clock clock_1 (.out(clock_1_out));
  and and_1 (out_4, or_2_out, not_1_out);
  S_R_Flip_Flop s_r_ff_1 (
    .S(in_1), .R(in_2), .Q(Q), .Qn(Nicht_Q), .preset(in_1), .reset(in_2), .en(in_2));  // open: clk
  nor nor_1 (Niht_Q, in_1, Q_2);
  nor nor_2 (Q_2, Niht_Q, in_2);
  nor nor_3 (Niht_Q_2, and_2_out, Q_3);
  buf and_2 (and_2_out, in_1);  // AND_Gate
  buf and_3 (and_3_out, in_2);  // AND_Gate
  nor nor_4 (Q_3, Niht_Q_2, and_3_out);
  J_K_Flip_Flop j_k_ff_1 ();  // open: J, clk, K, Q, Qn, preset, en, reset
  T_Flip_Flop t_ff_1 ();  // open: clk, T, Q, Qn, preset, reset, en
  D_Flip_Flop d_ff_1 ();  // open: clk, D, Q, Qn, preset, en, reset
endmodule
