// Logisim project orangensaft.circ as structural Verilog: 1 circuit, main circuit main
module main (
  input  in_1,
  output fehlen_200,
  output A1,
  output fehlen_150,
  output fehlen_100,
  output A2,
  output fehlen_50,
  output fehlen_0__Flasche,
  output Z1,
  output Z2
);

  wire and_1_out, and_2_out, and_3_out, and_4_out, and_5_out, and_6_out, and_7_out, and_8_out, and_9_out,
       and_10_out, and_11_out, clock_1_out, j_k_ff_1_q, j_k_ff_2_q, j_k_ff_3_q, j_k_ff_4_q, j_k_ff_5_q,
       not_1_out, not_2_out, not_3_out, not_4_out, not_5_out, not_6_out, not_7_out, not_8_out;

  not not_1 (not_1_out, j_k_ff_2_q);
  not not_2 (not_2_out, j_k_ff_1_q);
  not not_3 (not_3_out, in_1);
  and and_1 (and_1_out, not_2_out, not_3_out);
  and and_2 (and_2_out, not_1_out, not_2_out);
  and and_3 (and_3_out, in_1, j_k_ff_2_q, not_2_out);
  and and_4 (and_4_out, not_1_out, not_3_out);
  and and_5 (and_5_out, not_3_out, not_1_out, j_k_ff_1_q);
  and and_6 (and_6_out, j_k_ff_2_q, not_2_out);
  and and_7 (and_7_out, in_1, not_2_out);
  and and_8 (and_8_out, in_1, j_k_ff_2_q, not_2_out);
  and and_9 (and_9_out, not_1_out, not_3_out);
  or or_1 (A1, and_1_out, and_2_out);
  or or_2 (A2, and_3_out, and_4_out);
  or or_3 (Z1, and_5_out, and_6_out, and_7_out);
  Clock clock_1 (.out(clock_1_out));
  or or_4 (Z2, and_8_out, and_9_out);
  not not_4 (not_4_out, Z1);
  not not_5 (not_5_out, Z2);
  J_K_Flip_Flop j_k_ff_1 (
    .J(Z1), .clk(clock_1_out), .K(not_4_out), .Q(j_k_ff_1_q), .reset(j_k_ff_5_q));  // open: Qn, preset, en
  J_K_Flip_Flop j_k_ff_2 (
    .J(Z2), .clk(clock_1_out), .K(not_5_out), .Q(j_k_ff_2_q), .reset(j_k_ff_5_q));  // open: Qn, preset, en
  not not_6 (not_6_out, A1);
  not not_7 (not_7_out, A2);
  J_K_Flip_Flop j_k_ff_3 (.J(A1), .clk(clock_1_out), .K(not_6_out), .Q(j_k_ff_3_q));  // open: Qn, preset, en, reset
  J_K_Flip_Flop j_k_ff_4 (.J(A2), .clk(clock_1_out), .K(not_7_out), .Q(j_k_ff_4_q));  // open: Qn, preset, en, reset
  not not_8 (not_8_out, fehlen_0__Flasche);
  and and_10 (and_10_out, j_k_ff_3_q, j_k_ff_5_q, ~j_k_ff_4_q);  // AND_Gate
  or or_5 (fehlen_200, and_10_out, and_11_out);
  and and_11 (and_11_out, j_k_ff_4_q, j_k_ff_5_q, j_k_ff_3_q);
  and and_12 (fehlen_150, j_k_ff_3_q, ~j_k_ff_5_q, j_k_ff_4_q);  // AND_Gate
  and and_13 (fehlen_100, ~j_k_ff_4_q, ~j_k_ff_5_q, j_k_ff_3_q);  // AND_Gate
  and and_14 (fehlen_50, ~j_k_ff_3_q, j_k_ff_4_q);  // AND_Gate
  and and_15 (fehlen_0__Flasche, ~j_k_ff_3_q, ~j_k_ff_4_q);  // AND_Gate
  J_K_Flip_Flop j_k_ff_5 (
    .J(fehlen_0__Flasche), .clk(clock_1_out), .K(not_8_out), .Q(j_k_ff_5_q));  // open: Qn, preset, en, reset
endmodule
