// Logisim project parallel.circ as structural Verilog: 1 circuit, main circuit main
module main (
  input  in_1,
  input  in_2,
  input  in_3,
  input  in_4,
  input  in_5,
  output E0,
  output E0_2
);

  wire and_1_out, and_2_out, and_3_out, and_4_out, and_5_out, and_6_out, or_1_out, or_2_out, xor_1_out,
       xor_3_out;

  or or_1 (or_1_out, and_1_out, and_2_out, and_3_out);
  and and_1 (and_1_out, or_2_out, in_5);
  and and_2 (and_2_out, in_5, in_4);
  and and_3 (and_3_out, in_4, or_2_out);
  xor xor_1 (xor_1_out, in_5, or_2_out);
  xor xor_2 (E0_2, in_4, xor_1_out);
  or or_2 (or_2_out, and_4_out, and_5_out, and_6_out);
  and and_4 (and_4_out, in_3, in_2);
  and and_5 (and_5_out, in_2, in_1);
  and and_6 (and_6_out, in_1, in_3);
  xor xor_3 (xor_3_out, in_2, in_3);
  xor xor_4 (E0, in_1, xor_3_out);
endmodule
