// Logisim project schiebe_addierer.circ as structural Verilog: 1 circuit, main circuit main
module main (
  input  in_1,
  input  in_2,
  input  in_3,
  input  in_4,
  output out_5,
  output out_6,
  output out_7,
  output out_8,
  output out_9,
  output out_10,
  output out_11,
  output out_12,
  output out_13,
  output out_14,
  output out_15,
  output out_16,
  output out_17,
  output out_18,
  output out_19,
  output out_20,
  output out_21,
  output out_22,
  output out_23,
  output out_24,
  output out_25,
  output out_26,
  output out_27,
  output out_28,
  output out_29,
  output out_30,
  output out_31,
  output out_32,
  output out_33,
  output out_34,
  output out_35,
  output out_36,
  output out_37
);

  wire adder_1_cout, adder_1_out, clock_1_out, not_1_out, not_2_out, not_3_out, not_4_out, not_5_out,
       not_6_out, not_7_out, not_8_out, s_r_ff_1_qn, s_r_ff_2_qn, s_r_ff_3_qn, s_r_ff_4_qn, s_r_ff_5_qn,
       s_r_ff_6_qn, s_r_ff_7_qn, s_r_ff_8_qn, s_r_ff_9_qn, s_r_ff_10_qn, s_r_ff_11_qn, s_r_ff_12_qn,
       s_r_ff_13_qn, s_r_ff_14_qn, s_r_ff_15_qn, s_r_ff_16_qn, s_r_ff_17_qn, s_r_ff_22_q, s_r_ff_23_q,
       s_r_ff_24_qn, s_r_ff_25_qn, s_r_ff_26_qn, s_r_ff_27_qn, s_r_ff_28_qn, s_r_ff_29_qn, s_r_ff_30_qn,
       s_r_ff_31_qn, s_r_ff_32_qn, s_r_ff_33_qn, subtractor_1_bout, subtractor_1_out;

  Clock clock_1 (.out(clock_1_out));
  S_R_Flip_Flop s_r_ff_1 (
    .S(in_1), .clk(clock_1_out), .R(not_1_out), .Q(out_5), .Qn(s_r_ff_1_qn));  // open: preset, reset, en
  not not_1 (not_1_out, in_1);
  not not_2 (not_2_out, in_2);
  S_R_Flip_Flop s_r_ff_2 (
    .S(in_3), .clk(clock_1_out), .R(not_3_out), .Q(out_22), .Qn(s_r_ff_2_qn));  // open: preset, reset, en
  not not_3 (not_3_out, in_3);
  S_R_Flip_Flop s_r_ff_3 (
    .S(in_4), .clk(clock_1_out), .R(not_4_out), .Q(out_33), .Qn(s_r_ff_3_qn));  // open: preset, reset, en
  not not_4 (not_4_out, in_4);
  S_R_Flip_Flop s_r_ff_4 (
    .S(out_5), .clk(clock_1_out), .R(s_r_ff_1_qn), .Q(out_6), .Qn(s_r_ff_4_qn));  // open: preset, reset, en
  S_R_Flip_Flop s_r_ff_5 (
    .S(in_2), .clk(clock_1_out), .R(not_2_out), .Q(out_17), .Qn(s_r_ff_5_qn));  // open: preset, reset, en
  S_R_Flip_Flop s_r_ff_6 (
    .S(out_22), .clk(clock_1_out), .R(s_r_ff_2_qn), .Q(out_23), .Qn(s_r_ff_6_qn));  // open: preset, reset, en
  S_R_Flip_Flop s_r_ff_7 (
    .S(out_33), .clk(clock_1_out), .R(s_r_ff_3_qn), .Q(out_34), .Qn(s_r_ff_7_qn));  // open: preset, reset, en
  S_R_Flip_Flop s_r_ff_8 (
    .S(out_6), .clk(clock_1_out), .R(s_r_ff_4_qn), .Q(out_7), .Qn(s_r_ff_8_qn));  // open: preset, reset, en
  S_R_Flip_Flop s_r_ff_9 (
    .S(out_7), .clk(clock_1_out), .R(s_r_ff_8_qn), .Q(out_8), .Qn(s_r_ff_9_qn));  // open: preset, reset, en
  S_R_Flip_Flop s_r_ff_10 (
    .S(out_17), .clk(clock_1_out), .R(s_r_ff_5_qn), .Q(out_18), .Qn(s_r_ff_10_qn));  // open: preset, reset, en
  S_R_Flip_Flop s_r_ff_11 (
    .S(out_18), .clk(clock_1_out), .R(s_r_ff_10_qn), .Q(out_19), .Qn(s_r_ff_11_qn));  // open: preset, reset, en
  S_R_Flip_Flop s_r_ff_12 (
    .S(out_23), .clk(clock_1_out), .R(s_r_ff_6_qn), .Q(out_24), .Qn(s_r_ff_12_qn));  // open: preset, reset, en
  S_R_Flip_Flop s_r_ff_13 (
    .S(out_34), .clk(clock_1_out), .R(s_r_ff_7_qn), .Q(out_35), .Qn(s_r_ff_13_qn));  // open: preset, reset, en
  S_R_Flip_Flop s_r_ff_14 (
    .S(out_8), .clk(clock_1_out), .R(s_r_ff_9_qn), .Q(out_9), .Qn(s_r_ff_14_qn));  // open: preset, reset, en
  S_R_Flip_Flop s_r_ff_15 (
    .S(out_19), .clk(clock_1_out), .R(s_r_ff_11_qn), .Q(out_20), .Qn(s_r_ff_15_qn));  // open: preset, reset, en
  S_R_Flip_Flop s_r_ff_16 (
    .S(out_24), .clk(clock_1_out), .R(s_r_ff_12_qn), .Q(out_25), .Qn(s_r_ff_16_qn));  // open: preset, reset, en
  S_R_Flip_Flop s_r_ff_17 (
    .S(out_35), .clk(clock_1_out), .R(s_r_ff_13_qn), .Q(out_36), .Qn(s_r_ff_17_qn));  // open: preset, reset, en
  S_R_Flip_Flop s_r_ff_18 (.S(out_9), .clk(clock_1_out), .R(s_r_ff_14_qn), .Q(out_10));  // open: Qn, preset, reset, en
  S_R_Flip_Flop s_r_ff_19 (.S(out_20), .clk(clock_1_out), .R(s_r_ff_15_qn), .Q(out_21));  // open: Qn, preset, reset, en
  S_R_Flip_Flop s_r_ff_20 (.S(out_25), .clk(clock_1_out), .R(s_r_ff_16_qn), .Q(out_26));  // open: Qn, preset, reset, en
  S_R_Flip_Flop s_r_ff_21 (.S(out_36), .clk(clock_1_out), .R(s_r_ff_17_qn), .Q(out_37));  // open: Qn, preset, reset, en
  Adder #(.width(1)) adder_1 (.a(out_10), .b(out_21), .out(adder_1_out), .cin(s_r_ff_23_q), .cout(adder_1_cout));
  not not_5 (not_5_out, adder_1_cout);
  Subtractor #(.width(1)) subtractor_1 (
    .a(out_26), .b(out_37), .out(subtractor_1_out), .bin(s_r_ff_22_q), .bout(subtractor_1_bout));
  S_R_Flip_Flop s_r_ff_22 (
    .S(subtractor_1_bout), .clk(clock_1_out), .R(not_6_out), .Q(s_r_ff_22_q));  // open: Qn, preset, reset, en
  not not_6 (not_6_out, subtractor_1_bout);
  not not_7 (not_7_out, adder_1_out);
  S_R_Flip_Flop s_r_ff_23 (
    .S(adder_1_cout), .clk(clock_1_out), .R(not_5_out), .Q(s_r_ff_23_q));  // open: Qn, preset, reset, en
  not not_8 (not_8_out, subtractor_1_out);
  S_R_Flip_Flop s_r_ff_24 (
    .S(adder_1_out), .clk(clock_1_out), .R(not_7_out), .Q(out_11), .Qn(s_r_ff_24_qn));  // open: preset, reset, en
  S_R_Flip_Flop s_r_ff_25 (
    .S(subtractor_1_out), .clk(clock_1_out), .R(not_8_out), .Q(out_27), .Qn(s_r_ff_25_qn));  // open: preset, reset, en
  S_R_Flip_Flop s_r_ff_26 (
    .S(out_11), .clk(clock_1_out), .R(s_r_ff_24_qn), .Q(out_12), .Qn(s_r_ff_26_qn));  // open: preset, reset, en
  S_R_Flip_Flop s_r_ff_27 (
    .S(out_27), .clk(clock_1_out), .R(s_r_ff_25_qn), .Q(out_28), .Qn(s_r_ff_27_qn));  // open: preset, reset, en
  S_R_Flip_Flop s_r_ff_28 (
    .S(out_28), .clk(clock_1_out), .R(s_r_ff_27_qn), .Q(out_29), .Qn(s_r_ff_28_qn));  // open: preset, reset, en
  S_R_Flip_Flop s_r_ff_29 (
    .S(out_12), .clk(clock_1_out), .R(s_r_ff_26_qn), .Q(out_13), .Qn(s_r_ff_29_qn));  // open: preset, reset, en
  S_R_Flip_Flop s_r_ff_30 (
    .S(out_29), .clk(clock_1_out), .R(s_r_ff_28_qn), .Q(out_30), .Qn(s_r_ff_30_qn));  // open: preset, reset, en
  S_R_Flip_Flop s_r_ff_31 (
    .S(out_14), .clk(clock_1_out), .R(s_r_ff_32_qn), .Q(out_15), .Qn(s_r_ff_31_qn));  // open: preset, reset, en
  S_R_Flip_Flop s_r_ff_32 (
    .S(out_13), .clk(clock_1_out), .R(s_r_ff_29_qn), .Q(out_14), .Qn(s_r_ff_32_qn));  // open: preset, reset, en
  S_R_Flip_Flop s_r_ff_33 (
    .S(out_30), .clk(clock_1_out), .R(s_r_ff_30_qn), .Q(out_31), .Qn(s_r_ff_33_qn));  // open: preset, reset, en
  S_R_Flip_Flop s_r_ff_34 (.S(out_15), .clk(clock_1_out), .R(s_r_ff_31_qn), .Q(out_16));  // open: Qn, preset, reset, en
  S_R_Flip_Flop s_r_ff_35 (.S(out_31), .clk(clock_1_out), .R(s_r_ff_33_qn), .Q(out_32));  // open: Qn, preset, reset, en
endmodule
