// Logisim project test.circ as structural Verilog: 1 circuit, main circuit main
module main (
  input  in_1,
  input  in_2,
  input  in_3,
  input  in_4
);

  wire keyboard_1_avail, nand_1_out, odd_parity_1_out, shift_register_1_q0, shift_register_1_q1,
       shift_register_1_q2, shift_register_1_q3, shift_register_1_q4, shift_register_1_q5,
       shift_register_1_q6, shift_register_1_q7, t_ff_1_q, t_ff_1_qn, undriven;
  wire [3:0] joystick_1_x;
  wire [6:0] keyboard_1_data;

  Joystick joystick_1 (.x(joystick_1_x), .y(joystick_1_x));
  Keyboard keyboard_1 (.avail(keyboard_1_avail), .data(keyboard_1_data));  // open: clk, re, clr
  Hex_Digit_Display hex_digit_display_1 (.value(joystick_1_x), .dp(in_2));
  DotMatrix dotmatrix_1 (.col0(keyboard_1_data), .col2(keyboard_1_data), .col4(keyboard_1_data));  // open: col1, col3
  Shift_Register shift_register_1 (
    .load(in_1), .clr(undriven), .d0(in_2), .q0(shift_register_1_q0), .d1(in_3), .q1(shift_register_1_q1),
    .q2(shift_register_1_q2), .q3(shift_register_1_q3), .q4(shift_register_1_q4), .q5(shift_register_1_q5),
    .q6(shift_register_1_q6), .q7(shift_register_1_q7));  // open: shift, in, clk, out, d2, d3, d4, d5, d6, d7
  T_Flip_Flop t_ff_1 (.Q(t_ff_1_q), .Qn(t_ff_1_qn), .preset(in_1), .reset(in_4));  // open: clk, T, en
  nand nand_1 (nand_1_out, in_1, in_2, in_3);
  LED led_1 (.in(nand_1_out));
  xor odd_parity_1 (odd_parity_1_out, in_1, shift_register_1_q5, shift_register_1_q7, shift_register_1_q6, shift_register_1_q4, shift_register_1_q3);
endmodule
