// Logisim project volladdierer-mit-technik.circ as structural Verilog: 1 circuit, main circuit main
module main (
  input  a,
  input  b,
  input  u,
  input  AND,
  input  OR,
  input  in_6,
  input  in_7,
  input  NOT,
  output ueb,
  output erg
);

  wire pull_resistor_1_node, pull_resistor_2_node, pull_resistor_3_node, pull_resistor_4_node,
       pull_resistor_5_node, pull_resistor_6_node, pull_resistor_11_node, pull_resistor_12_node,
       pull_resistor_13_node, pull_resistor_16_node, pull_resistor_21_node, transistor_7_out,
       transistor_8_out, transistor_9_out, transistor_10_out, transistor_14_out, transistor_15_out,
       transistor_17_out, transistor_18_out;

  Pull_Resistor pull_resistor_1 (.node(pull_resistor_1_node));
  Transistor #(.\type ("n")) transistor_1 (.in(OR), .out(pull_resistor_1_node), .gate(AND));
  Pull_Resistor #(.pull(1)) pull_resistor_2 (.node(pull_resistor_2_node));
  Transistor transistor_2 (.in(in_7), .out(pull_resistor_2_node), .gate(in_6));
  Pull_Resistor #(.pull(1)) pull_resistor_3 (.node(pull_resistor_3_node));
  Transistor #(.\type ("n")) transistor_3 (.in(1'b0), .out(pull_resistor_3_node), .gate(NOT));
  Pull_Resistor #(.pull(1)) pull_resistor_4 (.node(pull_resistor_4_node));
  Pull_Resistor #(.pull(1)) pull_resistor_5 (.node(pull_resistor_5_node));
  Transistor #(.\type ("n")) transistor_4 (.in(1'b0), .out(pull_resistor_5_node), .gate(b));
  Transistor #(.\type ("n")) transistor_5 (.in(1'b0), .out(pull_resistor_4_node), .gate(a));
  Pull_Resistor #(.pull(1)) pull_resistor_6 (.node(pull_resistor_6_node));
  Transistor #(.\type ("n")) transistor_6 (.in(1'b0), .out(pull_resistor_6_node), .gate(u));
  Transistor transistor_7 (.in(b), .out(transistor_7_out), .gate(u));
  Pull_Resistor #(.pull(1)) pull_resistor_7 (.node(transistor_7_out));
  Transistor transistor_8 (.in(a), .out(transistor_8_out), .gate(u));
  Pull_Resistor #(.pull(1)) pull_resistor_8 (.node(transistor_8_out));
  Transistor transistor_9 (.in(a), .out(transistor_9_out), .gate(b));
  Pull_Resistor #(.pull(1)) pull_resistor_9 (.node(transistor_9_out));
  Transistor #(.\type ("n")) transistor_10 (.in(pull_resistor_4_node), .out(transistor_10_out), .gate(b));
  Pull_Resistor pull_resistor_10 (.node(transistor_10_out));
  Pull_Resistor #(.pull(1)) pull_resistor_11 (.node(pull_resistor_11_node));
  Transistor transistor_11 (.in(pull_resistor_12_node), .out(pull_resistor_11_node), .gate(transistor_10_out));
  Pull_Resistor pull_resistor_12 (.node(pull_resistor_12_node));
  Transistor #(.\type ("n")) transistor_12 (.in(pull_resistor_5_node), .out(pull_resistor_12_node), .gate(a));
  Pull_Resistor pull_resistor_13 (.node(pull_resistor_13_node));
  Transistor #(.\type ("n")) transistor_13 (.in(pull_resistor_5_node), .out(pull_resistor_13_node), .gate(a));
  Transistor transistor_14 (.in(transistor_15_out), .out(transistor_14_out), .gate(pull_resistor_13_node));
  Pull_Resistor #(.pull(1)) pull_resistor_14 (.node(transistor_14_out));
  Transistor #(.\type ("n")) transistor_15 (.in(pull_resistor_4_node), .out(transistor_15_out), .gate(b));
  Pull_Resistor pull_resistor_15 (.node(transistor_15_out));
  Pull_Resistor pull_resistor_16 (.node(pull_resistor_16_node));
  Transistor #(.\type ("n")) transistor_16 (
    .in(transistor_8_out), .out(pull_resistor_16_node), .gate(transistor_7_out));
  Transistor #(.\type ("n")) transistor_17 (
    .in(pull_resistor_6_node), .out(transistor_17_out), .gate(pull_resistor_11_node));
  Pull_Resistor pull_resistor_17 (.node(transistor_17_out));
  Transistor #(.\type ("n")) transistor_18 (.in(1'b0), .out(transistor_18_out), .gate(transistor_14_out));
  Pull_Resistor #(.pull(1)) pull_resistor_18 (.node(transistor_18_out));
  Pull_Resistor pull_resistor_19 (.node(ueb));
  Transistor #(.\type ("n")) transistor_19 (.in(transistor_9_out), .out(ueb), .gate(pull_resistor_16_node));
  Pull_Resistor #(.pull(1)) pull_resistor_20 (.node(erg));
  Transistor transistor_20 (.in(pull_resistor_21_node), .out(erg), .gate(transistor_17_out));
  Pull_Resistor pull_resistor_21 (.node(pull_resistor_21_node));
  Transistor #(.\type ("n")) transistor_21 (.in(u), .out(pull_resistor_21_node), .gate(transistor_18_out));
endmodule
