// Logisim project volladdierer.circ as structural Verilog: 1 circuit, main circuit main
module main (
  input  a,
  input  b,
  input  u,
  output Ueber,
  output Ergebnis
);

  wire not_1_out, not_2_out, or_1_out, or_2_out, or_3_out, u_out, xor_1_out;

  not not_1 (not_1_out, a);
  not u_u (u_out, u);
  not not_2 (not_2_out, b);
  or or_1 (or_1_out, b, u);
  or or_2 (or_2_out, a, u);
  and and_1 (Ueber, or_1_out, or_2_out, or_3_out);
  or or_3 (or_3_out, a, b);
  xor xor_1 (xor_1_out, a, b);
  xor xor_2 (Ergebnis, xor_1_out, u);
endmodule
